// Logisim project DevoirType.circ as structural Verilog: 1 circuit, main circuit main
module main (
  input  A,
  input  B,
  input  C
);

  wire not_1_out, not_2_out, not_3_out;

  not not_1 (not_1_out, A);
  not not_2 (not_2_out, B);
  not not_3 (not_3_out, C);

  // Notes on the sheet:
  //   A
  //   valeur
  //   S=
  //   S=
  //   S=
  //   1) remplir le table de vérité de S:
  //   B
  //   Forme normale conjonctive
  //   Forme Normale Disjonctive
  //   3) Simplifiez la forme normale disjontive
  //   4) Construire le circuit qui exprime la fonction S
  //   C
  //   2) Donner la forme normale conjontive de S et sa forme normale disjonctive
  //   S
  //   On se donne trois entrées de 1 bit  A, B et C qui représente un nombre écrit en base 2 sous la forme  ABC. L'objectif est de construire le circuit de la fonction S qui renvoie 1 si le nombre est un carré parfait sinon 0.
endmodule
